# Fritzing sketch Arduino_Drone (saved by Fritzing 0.8.7b)
breadboards: 1

parts:
  GY1 = MPU-6050 Board GY-521 [form="♀ (female)" package=THT]
  Parte1 = Arduino Nano (Rev3.0)
  U1 = AD5206 Digital Potentiometer [maximum_resistance=10kΩ package="DIP28 [THT]"]

nets (from the breadboard view):
  3V3: GY1.pin1, Parte1.3V3, U1.Vdd
  GND: GY1.pin2, Parte1.GND, U1.Gnd
  N1: GY1.pin3, Parte1.A5
  N2: GY1.pin4, Parte1.A4
  N3: Parte1.D10, U1.CS
  N4: Parte1.D11/MOSI, U1.SDI
  N5: Parte1.D13/SCK, U1.CLK
  N6: U1.B5, U1.W5, U1.A5
  N7: U1.B3, U1.W3, U1.A3

custom parts:
  MPU-6050 Board GY-521: Acelerometro y Giroscopio MPU-6050 Board GY-521
